# Fritzing sketch openSensor_01 (saved by Fritzing 0.9.2b)
breadboards: 1

parts:
  Composant1 = Arduino Nano (Rev3.0)
  NRF24L1 = NRF24L01
  U1 = TEMPERATURE-SENSOR [package=to-92]
  R1 = Resistor [tolerance=±5% resistance=4.7k package=THT]
  R2 = Photocell (LDR) [package=THT]
  R3 = Resistor [tolerance=±5% resistance=220 package=THT]
  Composant2 = FC-28 Soil Hygrometer Module - Probe
  Composant3 = FC-28 Soil Hygrometer Module
  Composant4 = FC-28 Soil Hygrometer Module - Probe
  Composant5 = FC-28 Soil Hygrometer Module

nets:
  GND: Composant1.GND, NRF24L1.GND, U1.GND, R1.Pin_1, R3.Pin_0, Composant3.GND, Composant5.GND
  N1: Composant1.D2, U1.ADJ, R1.Pin_0
  N2: Composant1.D9, NRF24L1.CE
  N3: Composant1.D10, NRF24L1.CSN
  N4: Composant1.D11/MOSI, NRF24L1.MOSI
  N5: Composant1.D12/MISO, NRF24L1.MISO
  5V: Composant1.5V, U1.VCC
  N6: Composant1.A2, Composant5.AO
  N7: Composant1.A1, Composant3.AO
  N8: Composant1.A0, R2.pin_0, R3.Pin_1
  VCC: Composant1.3V3, NRF24L1.VCC, R2.pin_1, Composant3.VCC, Composant5.VCC
  N9: Composant1.D13/SCK, NRF24L1.SCK
  N10: Composant2.POS, Composant3.POS
  N11: Composant2.NEG, Composant3.NEG
  N12: Composant4.POS, Composant5.POS
  N13: Composant4.NEG, Composant5.NEG

custom parts:
  NRF24L01: NRF24L01 module
  FC-28 Soil Hygrometer Module - Probe: The FC-28 is a soil hygrometer module that uses the Texas Instruments LM393 comparator chip to provide an analog measurement of soil humidity.
  FC-28 Soil Hygrometer Module: The FC-28 is a soil hygrometer module that uses the Texas Instruments LM393 comparator chip to provide an analog measurement of soil humidity. The digital output is high when soil moisture is over a certain threshold, as determined by adjusting the potentiometer.
